# Fritzing sketch Battery_Test (saved by Fritzing 1.0.2b)
breadboards: 1

parts:
  Mod1 = Raspberry Pi 4B
  U1 = LIPO-2000mAh [package=lipo-2000]
  Part1 = INA219 High Side DC Current Sensor Breakout [part_number=904]
  R1 = Resistor [tolerance=±5% power=1W resistance=56 package=THT]
  R2 = Resistor [tolerance=±5% power=1W resistance=56 package=THT]
  R3 = Resistor [tolerance=±5% power=1W resistance=56 package=THT]
  R4 = Resistor [tolerance=±5% power=1W resistance=56 package=THT]
  R5 = Resistor [tolerance=±5% power=1W resistance=56 package=THT]
  R6 = Resistor [tolerance=±5% power=1W resistance=56 package=THT]
  R7 = Resistor [tolerance=±5% power=1W resistance=56 package=THT]
  R8 = Resistor [tolerance=±5% power=1W resistance=56 package=THT]
  R9 = Resistor [tolerance=±5% power=1W resistance=56 package=THT]
  R10 = Resistor [tolerance=±5% power=1W resistance=56 package=THT]
  R11 = Resistor [tolerance=±5% power=1W resistance=56 package=THT]
  R12 = Resistor [tolerance=±5% power=1W resistance=56 package=THT]
  R13 = Resistor [tolerance=±5% power=1W resistance=56 package=THT]
  R14 = Resistor [tolerance=±5% power=1W resistance=56 package=THT]
  R15 = Resistor [tolerance=±5% power=1W resistance=56 package=THT]
  R16 = Resistor [tolerance=±5% power=1W resistance=56 package=THT]
  R17 = Resistor [tolerance=±5% power=1W resistance=56 package=THT]
  R18 = Resistor [tolerance=±5% power=1W resistance=56 package=THT]
  R19 = Resistor [tolerance=±5% power=1W resistance=56 package=THT]
  R20 = Resistor [tolerance=±5% power=1W resistance=56 package=THT]
  R21 = Resistor [tolerance=±5% power=1W resistance=56 package=THT]
  R22 = Resistor [tolerance=±5% power=1W resistance=56 package=THT]
  R23 = Resistor [tolerance=±5% power=1W resistance=56 package=THT]
  R24 = Resistor [tolerance=±5% power=1W resistance=56 package=THT]
  R25 = Resistor [tolerance=±5% power=1W resistance=56 package=THT]
  R30 = Resistor [tolerance=±5% power=1W resistance=56 package=THT]
  R31 = Resistor [tolerance=±5% power=1W resistance=56 package=THT]
  R32 = Resistor [tolerance=±5% power=1W resistance=56 package=THT]
  R33 = Resistor [tolerance=±5% power=1W resistance=56 package=THT]
  R34 = Resistor [tolerance=±5% power=1W resistance=56 package=THT]
  R35 = Resistor [tolerance=±5% power=1W resistance=56 package=THT]
  R36 = Resistor [tolerance=±5% power=1W resistance=56 package=THT]
  R37 = Resistor [tolerance=±5% power=1W resistance=56 package=THT]
  R38 = Resistor [tolerance=±5% power=1W resistance=56 package=THT]
  R39 = Resistor [tolerance=±5% power=1W resistance=56 package=THT]
  R40 = Resistor [tolerance=±5% power=1W resistance=56 package=THT]
  R41 = Resistor [tolerance=±5% power=1W resistance=56 package=THT]
  R42 = Resistor [tolerance=±5% power=1W resistance=56 package=THT]
  R43 = Resistor [tolerance=±5% power=1W resistance=56 package=THT]
  R44 = Resistor [tolerance=±5% power=1W resistance=56 package=THT]
  R45 = Resistor [tolerance=±5% power=1W resistance=56 package=THT]
  R46 = Resistor [tolerance=±5% power=1W resistance=56 package=THT]
  R47 = Resistor [tolerance=±5% power=1W resistance=56 package=THT]
  R48 = Resistor [tolerance=±5% power=1W resistance=56 package=THT]
  R49 = Resistor [tolerance=±5% power=1W resistance=56 package=THT]
  R50 = Resistor [tolerance=±5% power=1W resistance=56 package=THT]
  R51 = Resistor [tolerance=±5% power=1W resistance=56 package=THT]
  R52 = Resistor [tolerance=±5% power=1W resistance=56 package=THT]
  R53 = Resistor [tolerance=±5% power=1W resistance=56 package=THT]
  R54 = Resistor [tolerance=±5% power=1W resistance=56 package=THT]
  R55 = Resistor [tolerance=±5% power=1W resistance=56 package=THT]
  R56 = Resistor [tolerance=±5% power=1W resistance=56 package=THT]
  R57 = Resistor [tolerance=±5% power=1W resistance=56 package=THT]
  R58 = Resistor [tolerance=±5% power=1W resistance=56 package=THT]
  R59 = Resistor [tolerance=±5% power=1W resistance=56 package=THT]
  R60 = Resistor [tolerance=±5% power=1W resistance=56 package=THT]
  R61 = Resistor [tolerance=±5% power=1W resistance=56 package=THT]
  R62 = Resistor [tolerance=±5% power=1W resistance=56 package=THT]
  R63 = Resistor [tolerance=±5% power=1W resistance=56 package=THT]
  R64 = Resistor [tolerance=±5% power=1W resistance=56 package=THT]

nets:
  3V3: Mod1.3V3, Part1.VCC
  N1: Mod1.GPIO2, Part1.SDA
  N2: Mod1.GPIO3, Part1.SCL
  GND: Mod1.GND, U1.-, Part1.GND, R1.Pin_0, R14.Pin_0, R15.Pin_0, R16.Pin_0, R17.Pin_0, R18.Pin_0, R21.Pin_0, R23.Pin_0, R24.Pin_0, R25.Pin_0, R55.Pin_0, R56.Pin_0, R57.Pin_0, R58.Pin_0, R59.Pin_0, R60.Pin_0, R61.Pin_0, R62.Pin_0, R63.Pin_0, R64.Pin_0
  N3: U1.+, Part1.VIN-
  N4: Part1.VIN+, R2.Pin_1, R4.Pin_1, R5.Pin_1, R6.Pin_1, R7.Pin_1, R8.Pin_1, R20.Pin_1, R30.Pin_1, R31.Pin_1, R32.Pin_1, R35.Pin_1, R36.Pin_1, R37.Pin_1, R38.Pin_1, R39.Pin_1, R40.Pin_1, R41.Pin_1, R42.Pin_1, R43.Pin_1, R44.Pin_1
  N5: R1.Pin_1, R3.Pin_0
  N6: R2.Pin_0, R3.Pin_1
  N7: R4.Pin_0, R9.Pin_1
  N8: R5.Pin_0, R10.Pin_1
  N9: R6.Pin_0, R11.Pin_1
  N10: R7.Pin_0, R12.Pin_1
  N11: R8.Pin_0, R13.Pin_1
  N12: R9.Pin_0, R14.Pin_1
  N13: R10.Pin_0, R15.Pin_1
  N14: R11.Pin_0, R16.Pin_1
  N15: R12.Pin_0, R18.Pin_1
  N16: R13.Pin_0, R17.Pin_1
  N17: R19.Pin_0, R21.Pin_1
  N18: R19.Pin_1, R20.Pin_0
  N19: R22.Pin_0, R23.Pin_1
  N20: R22.Pin_1, R30.Pin_0
  N21: R24.Pin_1, R33.Pin_0
  N22: R25.Pin_1, R34.Pin_0
  N23: R31.Pin_0, R33.Pin_1
  N24: R32.Pin_0, R34.Pin_1
  N25: R35.Pin_0, R45.Pin_1
  N26: R36.Pin_0, R46.Pin_1
  N27: R37.Pin_0, R47.Pin_1
  N28: R38.Pin_0, R48.Pin_1
  N29: R39.Pin_0, R49.Pin_1
  N30: R40.Pin_0, R50.Pin_1
  N31: R41.Pin_0, R51.Pin_1
  N32: R42.Pin_0, R54.Pin_1
  N33: R43.Pin_0, R53.Pin_1
  N34: R44.Pin_0, R52.Pin_1
  N35: R45.Pin_0, R55.Pin_1
  N36: R46.Pin_0, R56.Pin_1
  N37: R47.Pin_0, R57.Pin_1
  N38: R48.Pin_0, R58.Pin_1
  N39: R49.Pin_0, R59.Pin_1
  N40: R50.Pin_0, R60.Pin_1
  N41: R51.Pin_0, R61.Pin_1
  N42: R52.Pin_0, R62.Pin_1
  N43: R53.Pin_0, R63.Pin_1
  N44: R54.Pin_0, R64.Pin_1

custom parts:
  INA219 High Side DC Current Sensor Breakout: This breakout board will solve all your power-monitoring problems. Instead of struggling with two multimeters, you can just use the handy INA219B chip on this breakout to both measure both the high side voltage and DC current draw over I2C with 1% precision. Most current-measuring devices such as our current panel meter are only good for low side measuring. That means that unless you want to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
