# Fritzing sketch RPM_Sensor_Schematic (saved by Fritzing 1.0.2b)
breadboards: 1

parts:
  Part1 = Arduino Uno (Rev3)
  S2 = Reed switch [package=THT]
  S3 = Reed switch [package=THT]
  R1 = Resistor [tolerance=±5% power=0.25W resistance=680 package=THT]
  R2 = Resistor [tolerance=±5% power=0.25W resistance=860 package=THT]
  S4 = Reed switch [package=THT]

nets:
  N1: Part1.D3_PWM, R1.Pin_0
  N2: Part1.D4, R2.Pin_0
  N3: Part1.5V, S2.pin_2, S3.pin_2
  N4: Part1.GND, R1.Pin_1, R2.Pin_1, S4.pin_1, S4.pin_2
